# Fritzing sketch ARDUINO5V_WITH_4844_schematic_atmega328 (saved by Fritzing 0.9.3b)
breadboards: 1

parts:
  SI4844 = IC, DIP package, 24 pins [chip_label=IC]
  UNO = Arduino Uno (Rev3)
  I2C_Multiplexer = Adafruit TCA9548A
  Sparkfun = Logic Level Converter
  R1 = Resistor [tolerance=±5% resistance=2.2k package=THT]
  R2 = Resistor [tolerance=±5% resistance=2.2k package=THT]

nets:
  N1: SI4844.pin2, Sparkfun.RX2_LV
  N2: SI4844.pin15, Sparkfun.RX_LV
  N3: SI4844.pin16, I2C_Multiplexer.0SDA, R1.Pin_1
  N4: SI4844.pin17, I2C_Multiplexer.0SCL, R2.Pin_1
  N5: UNO.A5/SCL, I2C_Multiplexer.INPUTSCL
  N6: UNO.D12/MISO, Sparkfun.RX_HV
  GND: UNO.GND, I2C_Multiplexer.GND, I2C_Multiplexer.A1
  N7: UNO.A4/SDA, I2C_Multiplexer.INPUTSDA
  N8: UNO.D2, Sparkfun.RX2_HV
  5V: UNO.5V, I2C_Multiplexer.VCC
  N9: I2C_Multiplexer.A0, I2C_Multiplexer.A2
  3.3V: Sparkfun.LV, R1.Pin_0, R2.Pin_0
  5V_2: Sparkfun.HV

notes:
  Making Arduino UNO (5V) and SI4844 work.
  Ricardo Lima Caratti - Oct, 2019

custom parts:
  Adafruit TCA9548A: You just found the perfect I2C sensor, and you want to wire up two or three or more of them to your Arduino when you realize "Uh oh, this chip has a fixed I2C address, and from what I know about I2C, you cannot have two devices with the same address on the same SDA/SCL pins!" Are you out of luck? You would be, if you didn't have this ultra-cool TCA9548A 1-to-8 I2C multiplexer! Finally, a way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
