# Fritzing sketch OLED_WITH_4844_schematic_Arduino (saved by Fritzing 0.9.3b)
breadboards: 1

parts:
  S2 = SWITCH-MOMENTARY-2 [package=tactile-pth]
  S3 = SWITCH-MOMENTARY-2 [package=tactile-pth]
  S1 = SWITCH-MOMENTARY-2 [package=tactile-pth]
  part = Arduino Pro Mini v13
  S4 = SWITCH-MOMENTARY-2 [package=tactile-pth]
  R1 = Resistor [tolerance=±5% resistance=10k package=THT]
  R2 = Resistor [tolerance=±5% resistance=10k package=THT]
  OLED = OLED 0.96" 128x64 I2C SSD1306

nets:
  GND: S2.1, S3.1, S1.1, part.GND, S4.1, OLED.GND
  N1: S2.2, part.D7
  N2: S3.2, part.D8
  N3: S1.2, part.D5_PWM
  3.3V: part.VCC, R1.Pin_1, R2.Pin_1, OLED.VCC
  --->>> SI4844 pin 16 -: part.A4, R2.Pin_0, OLED.SCA
  --->>> SI4844 pin 17 -: part.A5, R1.Pin_0, OLED.SCL
  D15 SI4844: part.D12/MISO
  N4: part.D6_PWM, S4.2
  D2 SI4844: part.D2

notes:
  Band
  Arduino, OLED, Buttons and Arduino connections.
  Ricardo Lima Caratti - Oct, 2019
  D8
  D7
  D6
  D5
  SI4844 Pin 2 (Interrupt)
  BAND UP
  BAND DOWN
  VOLUME UP
  VOLUME DOWN
