# Fritzing sketch OLED_WITH_4844_schematic_SI4844 (saved by Fritzing 0.9.3b)
breadboards: 1

parts:
  SI4844 = IC, DIP package, 24 pins [chip_label=IC]
  C1 = Capacitor [part_number=100nF package=cap-pth-small2]
  L1 = Inductor [part_number=AM package="1206 [SMD]"]
  C2 = Capacitor [part_number=470nF package=cap-pth-small2]
  ANT1 = Antenna [part_number=FM]
  L2 = Inductors [package=0603]
  R9 = Slide Potentiometer [maximum_resistance=100kΩ]
  C3 = Capacitor [part_number=4.7uF package=cap-pth-small2]
  C4 = Capacitor [part_number=4.7uF package=cap-pth-small2]
  Y1 = CRYSTAL [package=tc26h]
  C5 = Capacitor [part_number=22pF package=cap-pth-small2]
  C6 = Capacitor [part_number=22pF package=cap-pth-small2]

nets:
  D2 Arduino: SI4844.pin2
  N1: SI4844.pin3, R9.leg1
  N2: SI4844.pin4, R9.wiper
  N3: SI4844.pin8, ANT1.antenna_lead, L2.1
  N4: SI4844.pin9, SI4844.pin11
  GND: SI4844.pin10, SI4844.pin14, L1.pin_1, R9.leg2, C5.2, C6.2
  N5: SI4844.pin12, C2.1
  D12 Arduino: SI4844.pin15
  Arduino A4 SDA .: SI4844.pin16
  Arduino A5 SCL .: SI4844.pin17
  N6: SI4844.pin18, C6.1
  N7: SI4844.pin19, Y1.2, C5.1
  3.3V: SI4844.pin20, SI4844.pin21, C1.2
  N8: SI4844.pin22, C1.1
  N9: SI4844.pin23, C4.1
  N10: SI4844.pin24, C3.1
  N11: L1.pin_0, C2.2, L2.2
  Audio Left: C3.2
  Audio Right: C4.2

notes:
  SI4844 minimal circuit and Arduino connections
  Ricardo Lima Caratti - Oct, 2019
  Arduino D2 (Interrupt)
