# Fritzing sketch OLED_WITH_4844_schematic_atmega328 (saved by Fritzing 0.9.3b)
breadboards: 1

parts:
  S2 = SWITCH-MOMENTARY-2 [package=tactile-pth]
  S3 = SWITCH-MOMENTARY-2 [package=tactile-pth]
  S1 = SWITCH-MOMENTARY-2 [package=tactile-pth]
  part = Arduino Pro Mini v13
  S4 = SWITCH-MOMENTARY-2 [package=tactile-pth]
  SI4844 = IC, DIP package, 24 pins [chip_label=IC]
  C3 = Capacitor [part_number=100nF package=cap-pth-small2]
  L1 = Inductor [part_number=AM package="1206 [SMD]"]
  C7 = Capacitor [part_number=470nF package=cap-pth-small2]
  ANT1 = Antenna [part_number=FM]
  L2 = Inductors [package=0603]
  R3 = Slide Potentiometer [maximum_resistance=100kΩ]
  C5 = Capacitor [part_number=4.7uF package=cap-pth-small2]
  C4 = Capacitor [part_number=4.7uF package=cap-pth-small2]
  Y1 = CRYSTAL [package=tc26h]
  C1 = Capacitor [part_number=22pF package=cap-pth-small2]
  C2 = Capacitor [part_number=22pF package=cap-pth-small2]
  R1 = Resistor [tolerance=±5% resistance=10k package=THT]
  R2 = Resistor [tolerance=±5% resistance=10k package=THT]
  OLED = OLED 0.96" 128x64 I2C SSD1306
  C6 = Capacitor [part_number=100nF package=cap-pth-small2]

nets:
  GND: S2.1, S3.1, S1.1, part.GND, S4.1, SI4844.pin10, SI4844.pin14, R3.leg2, C1.2, C2.2, OLED.GND, C6.1
  N1: S2.2, part.D7
  N2: S3.2, part.D8
  N3: S1.2, part.D5_PWM
  3.3V: part.VCC, SI4844.pin5, SI4844.pin20, SI4844.pin21, C3.2, R1.Pin_1, R2.Pin_1, OLED.VCC
  --->>> SI4844 pin 16 -: part.A4, R2.Pin_0, OLED.SCA
  --->>> SI4844 pin 17 -: part.A5, R1.Pin_0, OLED.SCL
  D15 SI4844: part.D12/MISO
  N4: part.D6_PWM, S4.2
  D2 SI4844: part.D2
  D2 Arduino: SI4844.pin2
  N5: SI4844.pin3, R3.leg1
  N6: SI4844.pin4, R3.wiper
  N7: SI4844.pin8, ANT1.antenna_lead, L2.1
  N8: SI4844.pin9, SI4844.pin11
  N9: SI4844.pin12, C7.1
  N10: SI4844.pin13, L1.pin_1
  D12 Arduino: SI4844.pin15, C6.2
  Arduino A4 SDA .: SI4844.pin16
  Arduino A5 SCL .: SI4844.pin17
  N11: SI4844.pin18, C2.1
  N12: SI4844.pin19, Y1.2, C1.1
  N13: SI4844.pin22, C3.1
  N14: SI4844.pin23, C4.1
  N15: SI4844.pin24, C5.1
  N16: L1.pin_0, C7.2, L2.2
  Audio Left: C5.2
  Audio Right: C4.2

notes:
  Band
  OLED, SI4844, Buttons and Arduino connection.
  Ricardo Lima Caratti - Oct, 2019
  D8
  D7
  D6
  D5
  Arduino D2 (Interrupt)
  SI4844 Pin 2 (Interrupt)
  BAND UP
  BAND DOWN
  VOLUME UP
  VOLUME DOWN
