# Fritzing sketch schematic_SI4844 (saved by Fritzing 0.9.3b)
breadboards: 1

parts:
  SI4844 = IC, DIP package, 24 pins [chip_label=IC]
  C3 = Capacitor [part_number=100nF package=cap-pth-small2]
  L1 = Inductor [part_number=AM package="1206 [SMD]"]
  C7 = Capacitor [part_number=470nF package=cap-pth-small2]
  ANT1 = Antenna [part_number=FM]
  L2 = Inductors [package=0603]
  R3 = Slide Potentiometer [maximum_resistance=100kΩ]
  C5 = Capacitor [part_number=4.7uF package=cap-pth-small2]
  C4 = Capacitor [part_number=4.7uF package=cap-pth-small2]
  Y1 = CRYSTAL [package=tc26h]
  C1 = Capacitor [part_number=22pF package=cap-pth-small2]
  C2 = Capacitor [part_number=22pF package=cap-pth-small2]
  C6 = Capacitor [part_number=100nF package=cap-pth-small2]

nets:
  D2 Arduino: SI4844.pin2
  N1: SI4844.pin3, R3.leg1
  N2: SI4844.pin4, R3.wiper
  3.3V: SI4844.pin5, SI4844.pin20, SI4844.pin21, C3.2
  N3: SI4844.pin8, ANT1.antenna_lead, L2.1
  N4: SI4844.pin9, SI4844.pin11
  GND: SI4844.pin10, SI4844.pin14, R3.leg2, C1.2, C2.2, C6.1
  N5: SI4844.pin12, C7.1
  N6: SI4844.pin13, L1.pin_1
  D12 Arduino: SI4844.pin15, C6.2
  Arduino A4 SDA .: SI4844.pin16
  Arduino A5 SCL .: SI4844.pin17
  N7: SI4844.pin18, C2.1
  N8: SI4844.pin19, Y1.2, C1.1
  N9: SI4844.pin22, C3.1
  N10: SI4844.pin23, C4.1
  N11: SI4844.pin24, C5.1
  N12: L1.pin_0, C7.2, L2.2
  Audio Left: C5.2
  Audio Right: C4.2

notes:
  SI4844 minimal circuit.
  Ricardo Lima Caratti - Oct, 2019
  Arduino D2 (Interrupt)
