# Fritzing sketch schematic_attiny85 (saved by Fritzing 0.9.3b)
breadboards: 1

parts:
  R4 = Resistor [tolerance=±5% resistance=3.3k package="0402 [SMD]"]
  R5 = Resistor [tolerance=±5% resistance=3.3k package="0402 [SMD]"]
  part = attiny85 [package=dip]
  BAND_UP = SWITCH-MOMENTARY-2 [package=tactile-pth]
  BAND_DOWN = SWITCH-MOMENTARY-2 [package=tactile-pth]

nets:
  3.3V: R4.Pin_0, R5.Pin_0, part.Pin_8
  SI4844 pin 17 (SCL) ------: R4.Pin_1, part.Pin_7
  SI4844 pin 16 (SDA) ------: R5.Pin_1, part.Pin_5
  --- SI4844 pin 2 ---: part.Pin_2
  N1: part.Pin_3, BAND_UP.1
  GND: part.Pin_4, BAND_UP.2, BAND_DOWN.2
  N2: part.Pin_6, BAND_DOWN.1

notes:
  SI4845 AND ATTINY85
  This circuit uses internal pull up resource
  Ricardo Lima Caratti - JAN 2020
